# Fritzing sketch KuechenlichtAlex (saved by Fritzing 0.9.3b)

parts:
  Arduino_Nano = Arduino Nano (Rev3.0) (ICSP)
  IR-Modul = fc-51 [package=THT]
  Relay_Modul = RELAY [package=relay-t9a]
  R1 = Resistor [tolerance=±5% resistance=1.5k package="2010 [SMD]"]
  LDR = Photocell (LDR) [package=THT]

nets:
  N1: Arduino_Nano.GND, IR-Modul.pin2, Relay_Modul.COIL1, R1.Pin_1
  N2: Arduino_Nano.D2, IR-Modul.pin1
  N3: Arduino_Nano.D6, Relay_Modul.COIL2
  N4: Arduino_Nano.5V, IR-Modul.pin3, LDR.pin_0
  N5: Arduino_Nano.A3, R1.Pin_0, LDR.pin_1
